# Fritzing sketch WindSensorMKR (saved by Fritzing 0.9.9b)
circuit board: 8.8cm x 4.6cm

parts:
  R1 = Resistor [tolerance=±1% resistance=10k power=0.25 package=THT]
  R3 = Resistor [tolerance=±1% resistance=560k power=0.25 package=THT]
  R4 = Resistor [tolerance=±1% resistance=390k power=0.25 package=THT]
  C2 = Film/Foil Capacitor [capacitance=100nF voltage=35V package="5mm [THT, pp]"]
  C1 = Film/Foil Capacitor [capacitance=100nF voltage=35V package="5mm [THT, pp]"]
  ON/OFF = SPST Switch [package=switch-spdt_kit]
  D1 = Schottky Diode [part_number=1N5817 package="300 mil [THT]"]
  D2 = Schottky Diode [part_number=1N5817 package="300 mil [THT]"]
  +BAT- = Screw terminal - 2 pins [package=THT]
  D3 = Schottky Diode [part_number=1N5817 package="300 mil [THT]"]
  D4 = Schottky Diode [part_number=1N5817 package="300 mil [THT]"]
  R2 = Resistor [tolerance=±1% resistance=100k power=0.25 package=THT]
  +SOLAR- = Screw terminal - 2 pins [package=THT]
  R5 = Resistor [tolerance=±1% resistance=1k power=0.25 package=THT]
  R6 = Resistor [tolerance=±1% resistance=1k power=0.25 package=THT]
  TP4056 = TP4056 [chip_label=TP4056 package="DIP (Dual Inline) [THT]"]
  MKRFox1200 = Arduino MKR Fox 1200
  RJ11_MISOL = RJ11 Jack
  BME280 = BME280 Barometric Sensor
  ext_switch = female pin header, 2 pins [form="♀ (female)"]

nets:
  pinGirAdc: R1.Pin_0, C2.-, D2.cathode, D3.anode, R6.Pin_0, MKRFox1200.A6
  pinGirAlim: R1.Pin_1, D3.cathode, MKRFox1200.~5
  N1: R3.Pin_0, R4.Pin_1, MKRFox1200.A4
  Vbat: R3.Pin_1, +BAT-.pin1, TP4056.pin4
  GND: R4.Pin_0, C2.+, C1.+, D1.anode, D2.anode, +BAT-.pin2, +SOLAR-.pin2, TP4056.pin2, TP4056.pin5, TP4056.pin6, MKRFox1200.GND, RJ11_MISOL.2, RJ11_MISOL.3
  intPinAnemo: C1.-, D1.cathode, D4.anode, R2.Pin_1, R5.Pin_0, MKRFox1200.~4
  N2: ON/OFF.O, MKRFox1200.VIN, ext_switch.pin1
  N3: ON/OFF.P, TP4056.pin3, ext_switch.pin2
  Vcc: D4.cathode, R2.Pin_0, MKRFox1200.VCC
  N4: +SOLAR-.pin1, TP4056.pin1
  N5: R5.Pin_1, RJ11_MISOL.5
  N6: R6.Pin_1, RJ11_MISOL.4
  pinVccBME: MKRFox1200.9_SCK, BME280.VCC
  pinGndBME: MKRFox1200.10_MISO, BME280.GND
  SDA: MKRFox1200.11_SDA, BME280.SDA
  SCL: MKRFox1200.12_SCL, BME280.SCL

notes:
  yellow
  green
  red
  black
  WindSensorMKR1200

custom parts:
  TP4056: A DIP stand-in part for whatever IC you want. With 6 pins on a 300mil dual inline package (DIP) footprint.
  BME280 Barometric Sensor: Bosh BME280 pressure temperature humidity
